// Logisim project Ampelschaltung_Zustaende.circ as structural Verilog: 1 circuit, main circuit main
module main (
);

  wire and_1_out, and_2_out, and_3_out, and_4_out, and_5_out, and_6_out, and_7_out, and_8_out, and_9_out,
       and_10_out, and_11_out, and_12_out, and_13_out, and_14_out, and_15_out, and_16_out, and_17_out,
       and_18_out, button_1_out, clock_1_out, counter_1_carry, counter_2_carry, counter_3_carry,
       counter_5_carry, d_ff_1_q, d_ff_2_q, not_1_out, not_2_out, not_3_out, not_4_out, not_5_out, not_6_out,
       not_7_out, not_8_out, not_9_out, not_10_out, not_11_out, not_12_out, not_13_out, not_14_out,
       not_15_out, not_16_out, not_17_out, not_18_out, not_19_out, not_20_out, not_21_out, not_22_out,
       not_23_out, not_24_out, not_25_out, not_26_out, not_27_out, or_1_out, or_2_out, or_3_out, or_4_out,
       or_5_out, or_6_out;
  wire [2:0] counter_4_q;

  Button button_1 (.out(button_1_out));
  not not_1 (not_1_out, counter_4_q[1]);
  not not_2 (not_2_out, counter_4_q[0]);
  not not_3 (not_3_out, counter_4_q[2]);
  and and_1 (and_1_out, not_2_out, not_1_out, not_3_out);
  or or_1 (or_1_out, and_1_out, and_9_out);
  LED led_1 (.in(or_1_out));
  D_Flip_Flop d_ff_1 (.clk(button_1_out), .D(button_1_out), .Q(d_ff_1_q), .reset(or_1_out));  // open: Qn, preset, en
  not not_4 (not_4_out, d_ff_1_q);
  and and_2 (and_2_out, clock_1_out, not_4_out);
  Counter #(.width(9), .max('h1ff)) counter_1 (
    .count(and_2_out), .carry(counter_1_carry), .clk(and_2_out), .clr(counter_2_carry));  // open: load, D, Q
  Clock clock_1 (.out(clock_1_out));
  Counter #(.width(11), .max('h7ff)) counter_2 (
    .count(d_ff_1_q), .carry(counter_2_carry), .clk(clock_1_out), .clr(or_1_out));  // open: load, D, Q
  Counter #(.width(4), .max('hf)) counter_3 (
    .count(counter_1_carry), .carry(counter_3_carry), .clk(clock_1_out), .clr(counter_2_carry));  // open: load, D, Q
  or or_2 (or_2_out, counter_3_carry, counter_2_carry);
  not not_5 (not_5_out, counter_4_q[2]);
  not not_6 (not_6_out, counter_4_q[1]);
  not not_7 (not_7_out, counter_4_q[2]);
  and and_3 (and_3_out, not_7_out, not_6_out, counter_4_q[0]);
  Counter #(.width(3), .max('h7)) counter_4 (.Q(counter_4_q), .clk(or_2_out));  // open: load, D, count, carry, clr
  not not_8 (not_8_out, counter_4_q[2]);
  not not_9 (not_9_out, counter_4_q[0]);
  and and_4 (and_4_out, not_8_out, counter_4_q[1], counter_4_q[0]);
  and and_5 (and_5_out, not_5_out, counter_4_q[1], not_9_out);
  or or_3 (or_3_out, and_7_out, and_3_out, and_5_out, and_4_out, and_6_out, and_8_out);
  LED led_2 (.in(or_3_out));
  not not_10 (not_10_out, counter_4_q[1]);
  not not_11 (not_11_out, counter_4_q[1]);
  not not_12 (not_12_out, counter_4_q[0]);
  and and_6 (and_6_out, counter_4_q[2], not_10_out, not_12_out);
  and and_7 (and_7_out, counter_4_q[2], not_11_out, counter_4_q[0]);
  not not_13 (not_13_out, counter_4_q[0]);
  and and_8 (and_8_out, counter_4_q[2], counter_4_q[1], not_13_out);
  and and_9 (and_9_out, counter_4_q[2], counter_4_q[1], counter_4_q[0]);
  not not_14 (not_14_out, counter_4_q[0]);
  not not_15 (not_15_out, counter_4_q[1]);
  not not_16 (not_16_out, counter_4_q[2]);
  not not_17 (not_17_out, counter_4_q[1]);
  not not_18 (not_18_out, counter_4_q[2]);
  not not_19 (not_19_out, counter_4_q[0]);
  not not_20 (not_20_out, counter_4_q[2]);
  not not_21 (not_21_out, counter_4_q[0]);
  not not_22 (not_22_out, counter_4_q[2]);
  not not_23 (not_23_out, counter_4_q[1]);
  not not_24 (not_24_out, counter_4_q[0]);
  not not_25 (not_25_out, counter_4_q[1]);
  not not_26 (not_26_out, counter_4_q[2]);
  and and_10 (and_10_out, not_14_out, not_15_out, not_16_out);
  and and_11 (and_11_out, counter_4_q[0], not_17_out, not_18_out);
  and and_12 (and_12_out, not_19_out, counter_4_q[1], not_20_out);
  and and_13 (and_13_out, not_21_out, counter_4_q[1], not_22_out);
  and and_14 (and_14_out, counter_4_q[0], not_23_out, counter_4_q[2]);
  and and_15 (and_15_out, not_24_out, not_25_out, counter_4_q[2]);
  and and_16 (and_16_out, counter_4_q[0], counter_4_q[1], not_26_out);
  not not_27 (not_27_out, counter_4_q[0]);
  and and_17 (and_17_out, not_27_out, counter_4_q[1], counter_4_q[2]);
  and and_18 (and_18_out, counter_4_q[0], counter_4_q[1], counter_4_q[2]);
  Counter #(.width(10), .max('h3ff)) counter_5 (
    .count(and_13_out), .carry(counter_5_carry), .clk(clock_1_out), .clr(or_4_out));  // open: load, D, Q
  D_Flip_Flop d_ff_2 (
    .clk(counter_5_carry), .D(counter_5_carry), .Q(d_ff_2_q), .reset(or_4_out));  // open: Qn, preset, en
  or or_4 (or_4_out, and_15_out, and_16_out);
  or or_5 (or_5_out, and_17_out, and_18_out, and_10_out, and_11_out, and_12_out);
  or or_6 (or_6_out, d_ff_2_q, and_14_out);
  LED led_3 (.in(or_5_out));
  LED led_4 (.in(or_6_out));
  LED led_5 (.in(or_4_out));

  // Notes on the sheet:
  //   Taster An
  //   Taster Aus
  //   Grün
  //   Fußgänger
  //   Zustandszähler
  //   Rot
  //   Rot-Gelb
  //   Rot
  //   000 -> 1
  //   001 -> 1
  //   010 -> 1
  //   010 -> 1
  //   101 -> 1
  //   100 -> 1
  //   011 -> 1
  //   Gelb
  //   Grün
  //   Kraftfahrzeuge
endmodule
